# Fritzing sketch etchabot (saved by Fritzing 0.9.4)
breadboards: 1

parts:
  Part1 = Arduino Uno (Rev3)
  BREAKOUT1 = ULN2003A breakout board
  BREAKOUT2 = ULN2003A breakout board
  BT1 = Bluetooth HC-06u [package=THT]
  JACK1 = 2.1mm Barrel Jack with Terminal Block
  MOTOR1 = 28BYJ-48 Stepper Motor
  MOTOR2 = 28BYJ-48 Stepper Motor

nets:
  N1: Part1.D8, BREAKOUT1.In_2
  N2: Part1.D9_PWM, BREAKOUT1.In_1
  N3: Part1.D10_PWM/SS, BREAKOUT2.In_4
  N4: Part1.D11_PWM/MOSI, BREAKOUT2.In_3
  N5: Part1.D12/MISO, BREAKOUT2.In_2
  N6: Part1.D13/SCK, BREAKOUT2.In_1
  N7: Part1.D4, BT1.TXD
  N8: Part1.D5_PWM, BT1.RXD
  N9: Part1.D6_PWM, BREAKOUT1.In_4
  N10: Part1.D7, BREAKOUT1.In_3
  5V: Part1.5V, BT1.VCC
  GND: Part1.GND, BREAKOUT1.0V, BREAKOUT2.0V, BT1.GND
  +5V: Part1.VIN, BREAKOUT1.+5V, BREAKOUT2.+5V, JACK1.POS
  N11: BREAKOUT1.RED_wire, MOTOR2.RED
  N12: BREAKOUT1.ORANGE_wire, MOTOR2.ORANGE
  N13: BREAKOUT1.YELLOW_wire, MOTOR2.YELLOW
  N14: BREAKOUT1.PINK_wire, MOTOR2.PINK
  N15: BREAKOUT1.BLUE_wire, MOTOR2.BLUE
  N16: BREAKOUT2.RED_wire, MOTOR1.RED
  N17: BREAKOUT2.ORANGE_wire, MOTOR1.ORANGE
  N18: BREAKOUT2.YELLOW_wire, MOTOR1.YELLOW
  N19: BREAKOUT2.PINK_wire, MOTOR1.PINK
  N20: BREAKOUT2.BLUE_wire, MOTOR1.BLUE

custom parts:
  ULN2003A breakout board: ULN2003A 7-way Darlington Transistor Driver on breakoutboard
  Bluetooth HC-06u: Bluetooth HC-06 - face up, pins down 16.5mm x 37.5mm PCB
